// Logisim project ALU.circ as structural Verilog
module ALU (
  input  s2,
  input  s1,
  input  s0,
  input  a0,
  input  a1,
  input  a2,
  input  a3,
  input  a4,
  input  a5,
  input  a6,
  input  a7,
  input  b0,
  input  b1,
  input  b2,
  input  b3,
  input  b4,
  input  b5,
  input  b6,
  input  b7,
  output r0,
  output r1,
  output r2,
  output r3,
  output r4,
  output r5,
  output r6,
  output r7,
  output Overflow,
  output Division_by_zero
);

  Selection selection_1 (
    .in_4(a0), .in_5(a1), .in_6(a2), .in_7(a3), .in_8(a4), .in_9(a5), .in_10(a6), .in_11(a7), .in_12(b0),
    .in_13(b1), .in_14(b2), .in_15(b3), .in_16(b4), .in_17(b5), .in_18(b6), .in_19(b7), .in_1(s2), .in_2(s1),
    .in_3(s0), .out_20(r0), .out_21(r1), .out_22(r2), .out_23(r3), .out_24(r4), .out_25(r5), .out_26(r6),
    .out_27(r7), .out_28(Overflow), .out_29(Division_by_zero));
endmodule

// ALU
module Selection (
  input  in_1,
  input  in_2,
  input  in_3,
  input  in_4,
  input  in_5,
  input  in_6,
  input  in_7,
  input  in_8,
  input  in_9,
  input  in_10,
  input  in_11,
  input  in_12,
  input  in_13,
  input  in_14,
  input  in_15,
  input  in_16,
  input  in_17,
  input  in_18,
  input  in_19,
  output out_20,
  output out_21,
  output out_22,
  output out_23,
  output out_24,
  output out_25,
  output out_26,
  output out_27,
  output out_28,
  output out_29
);

  wire n8bit_adder_1_overflow, n8bit_divider_1_overflow, n8bit_multiplier_1_overflow,
       n8bit_subtractor_1_overflow, nor_1_out;
  wire [7:0] n8bit_adder_1_out_3, n8bit_divider_1_out_4, n8bit_divider_2_out_4, n8bit_multiplier_1_out_3,
       n8bit_subtractor_1_out_3;

  _8bit_Adder u_8bit_adder_1 (
    .in_1({in_11, in_10, in_9, in_8, in_7, in_6, in_5, in_4}),
    .in_2({in_19, in_18, in_17, in_16, in_15, in_14, in_13, in_12}), .out_3(n8bit_adder_1_out_3),
    .Overflow(n8bit_adder_1_overflow));  // open: Carry_Out
  _8bit_Subtractor u_8bit_subtractor_1 (
    .in_1({in_11, in_10, in_9, in_8, in_7, in_6, in_5, in_4}),
    .in_2({in_19, in_18, in_17, in_16, in_15, in_14, in_13, in_12}), .out_3(n8bit_subtractor_1_out_3),
    .Overflow(n8bit_subtractor_1_overflow));
  _8bit_Multiplier u_8bit_multiplier_1 (
    .in_1({in_11, in_10, in_9, in_8, in_7, in_6, in_5, in_4}),
    .in_2({in_19, in_18, in_17, in_16, in_15, in_14, in_13, in_12}), .out_3(n8bit_multiplier_1_out_3),
    .Overflow(n8bit_multiplier_1_overflow));
  _8bit_Divider u_8bit_divider_1 (
    .in_1({in_11, in_10, in_9, in_8, in_7, in_6, in_5, in_4}),
    .in_2({in_19, in_18, in_17, in_16, in_15, in_14, in_13, in_12}), .Option(1'b0),
    .out_4(n8bit_divider_1_out_4), .Overflow(n8bit_divider_1_overflow));
  _8bit_Divider u_8bit_divider_2 (
    .in_1({in_11, in_10, in_9, in_8, in_7, in_6, in_5, in_4}),
    .in_2({in_19, in_18, in_17, in_16, in_15, in_14, in_13, in_12}), .Option(1'b1),
    .out_4(n8bit_divider_2_out_4));  // open: Overflow
  Multiplexer #(.select(3), .width(8), .enable("false")) multiplexer_1 (
    .in0(n8bit_adder_1_out_3), .in1(n8bit_subtractor_1_out_3), .in2(n8bit_multiplier_1_out_3),
    .in3(n8bit_divider_1_out_4), .in4(n8bit_divider_2_out_4),
    .out({out_27, out_26, out_25, out_24, out_23, out_22, out_21, out_20}), .sel({in_1, in_2, in_3}));  // open: in5, in6, in7
  Multiplexer #(.select(3), .enable("false")) multiplexer_2 (
    .in0(n8bit_adder_1_overflow), .in1(n8bit_subtractor_1_overflow), .in2(n8bit_multiplier_1_overflow),
    .in3(n8bit_divider_1_overflow), .in4(1'b0), .out(out_28), .sel({in_1, in_2, in_3}));  // open: in5, in6, in7
  nor nor_1 (nor_1_out, in_12, in_13, in_14, in_15, in_16, in_17, in_18, in_19);
  Multiplexer #(.select(3), .enable("false")) multiplexer_3 (
    .in0(1'b0), .in1(1'b0), .in2(1'b0), .in3(nor_1_out), .in4(nor_1_out), .out(out_29),
    .sel({in_1, in_2, in_3}));  // open: in5, in6, in7
endmodule

// HA
module Half_Adder (
  input  in_1,
  input  in_2,
  output Sum,
  output Carry
);

  wire not_1_out, or_1_out;

  or or_1 (or_1_out, in_1, in_2);
  and and_1 (Carry, in_1, in_2);
  not not_1 (not_1_out, Carry);
  and and_2 (Sum, or_1_out, not_1_out);
endmodule

// FA
module Full_Adder (
  input  in_1,
  input  in_2,
  input  Carry_In,
  output Sum,
  output Carry_Out
);

  wire half_adder_1_carry, half_adder_1_sum, half_adder_2_carry;

  Half_Adder half_adder_1 (.in_1(in_1), .in_2(in_2), .Sum(half_adder_1_sum), .Carry(half_adder_1_carry));
  Half_Adder half_adder_2 (.in_1(half_adder_1_sum), .in_2(Carry_In), .Sum(Sum), .Carry(half_adder_2_carry));
  or or_1 (Carry_Out, half_adder_1_carry, half_adder_2_carry);
endmodule

// Add
module _8bit_Adder (
  input  [7:0] in_1,
  input  [7:0] in_2,
  output [7:0] out_3,
  output Carry_Out,
  output Overflow
);

  wire and_1_out, and_2_out, full_adder_1_carry_out, full_adder_2_carry_out, full_adder_3_carry_out,
       full_adder_4_carry_out, full_adder_5_carry_out, full_adder_6_carry_out, full_adder_7_carry_out,
       not_1_out, not_2_out, not_3_out;

  Full_Adder full_adder_1 (
    .in_1(1'b0), .in_2(in_1[0]), .Carry_In(in_2[0]), .Sum(out_3[0]), .Carry_Out(full_adder_1_carry_out));
  Full_Adder full_adder_2 (
    .in_1(full_adder_1_carry_out), .in_2(in_1[1]), .Carry_In(in_2[1]), .Sum(out_3[1]),
    .Carry_Out(full_adder_2_carry_out));
  Full_Adder full_adder_3 (
    .in_1(full_adder_2_carry_out), .in_2(in_1[2]), .Carry_In(in_2[2]), .Sum(out_3[2]),
    .Carry_Out(full_adder_3_carry_out));
  Full_Adder full_adder_4 (
    .in_1(full_adder_3_carry_out), .in_2(in_1[3]), .Carry_In(in_2[3]), .Sum(out_3[3]),
    .Carry_Out(full_adder_4_carry_out));
  Full_Adder full_adder_5 (
    .in_1(full_adder_4_carry_out), .in_2(in_1[4]), .Carry_In(in_2[4]), .Sum(out_3[4]),
    .Carry_Out(full_adder_5_carry_out));
  Full_Adder full_adder_6 (
    .in_1(full_adder_5_carry_out), .in_2(in_1[5]), .Carry_In(in_2[5]), .Sum(out_3[5]),
    .Carry_Out(full_adder_6_carry_out));
  Full_Adder full_adder_7 (
    .in_1(full_adder_6_carry_out), .in_2(in_1[6]), .Carry_In(in_2[6]), .Sum(out_3[6]),
    .Carry_Out(full_adder_7_carry_out));
  Full_Adder full_adder_8 (
    .in_1(full_adder_7_carry_out), .in_2(in_1[7]), .Carry_In(in_2[7]), .Sum(out_3[7]), .Carry_Out(Carry_Out));
  not not_1 (not_1_out, in_1[7]);
  and and_1 (and_1_out, out_3[7], not_1_out, not_2_out);
  not not_2 (not_2_out, in_2[7]);
  not not_3 (not_3_out, out_3[7]);
  and and_2 (and_2_out, not_3_out, in_1[7], in_2[7]);
  or or_1 (Overflow, and_1_out, and_2_out);
endmodule

// Inv
module Additive_Inverse (
  input  [7:0] in_1,
  output [7:0] out_2,
  output Overflow
);

  wire [7:0] not_1_out;

  assign not_1_out = ~in_1;  // NOT_Gate not_1, 8 bits wide
  _8bit_Adder u_8bit_adder_1 (.in_1(not_1_out), .in_2(8'h1), .out_3(out_2), .Overflow(Overflow));  // open: Carry_Out
endmodule

// Sub
module _8bit_Subtractor (
  input  [7:0] in_1,
  input  [7:0] in_2,
  output [7:0] out_3,
  output Overflow
);

  wire additive_inverse_1_overflow, n8bit_adder_1_overflow;
  wire [7:0] additive_inverse_1_out_2;

  Additive_Inverse additive_inverse_1 (
    .in_1(in_2), .out_2(additive_inverse_1_out_2), .Overflow(additive_inverse_1_overflow));
  _8bit_Adder u_8bit_adder_1 (
    .in_1(in_1), .in_2(additive_inverse_1_out_2), .out_3(out_3), .Overflow(n8bit_adder_1_overflow));  // open: Carry_Out
  xor xor_1 (Overflow, n8bit_adder_1_overflow, additive_inverse_1_overflow);
endmodule

// Abs
module Absolute_Value (
  input  [7:0] in_1,
  output [7:0] out_2,
  output Is_it_negative
);

  wire not_1_out;
  wire [7:0] additive_inverse_1_out_2;

  Additive_Inverse additive_inverse_1 (.in_1(in_1), .out_2(additive_inverse_1_out_2));  // open: Overflow
  not not_1 (not_1_out, in_1[7]);
  Multiplexer #(.width(8), .enable("false")) multiplexer_1 (
    .in0(additive_inverse_1_out_2), .in1(in_1), .out(out_2), .sel(not_1_out));

  assign Is_it_negative = in_1[7];
endmodule

// Shift
module _7bit_Shifter (
  input  [7:0] in_1,
  input  [3:0] in_2,
  output [7:0] out_3,
  output Overflow
);

  wire [15:8] shifter_1_out;

  Shifter #(.width(16)) shifter_1 (.in({{8{1'b0}}, in_1}), .\dist (in_2), .out({shifter_1_out, out_3}));
  or or_1 (Overflow, out_3[7], shifter_1_out[8], shifter_1_out[9], shifter_1_out[10], shifter_1_out[11], shifter_1_out[12], shifter_1_out[13], shifter_1_out[14], shifter_1_out[15]);
endmodule

// Mulx1
module _8x1_Multiplier (
  input  in_1,
  input  [7:0] in_2,
  output [7:0] out_3
);

  and and_1 (out_3[0], in_2[0], in_1);
  and and_2 (out_3[1], in_2[1], in_1);
  and and_3 (out_3[2], in_2[2], in_1);
  and and_4 (out_3[3], in_2[3], in_1);
  and and_5 (out_3[4], in_2[4], in_1);
  and and_6 (out_3[5], in_2[5], in_1);
  and and_7 (out_3[6], in_2[6], in_1);
  and and_8 (out_3[7], in_2[7], in_1);
endmodule

// Mult
module _8bit_Multiplier (
  input  [7:0] in_1,
  input  [7:0] in_2,
  output [7:0] out_3,
  output Overflow
);

  wire absolute_value_1_is_it_negative, absolute_value_2_is_it_negative, additive_inverse_1_overflow,
       and_1_out, n7bit_shifter_1_overflow, n7bit_shifter_2_overflow, n7bit_shifter_3_overflow,
       n7bit_shifter_4_overflow, n7bit_shifter_5_overflow, n7bit_shifter_6_overflow,
       n7bit_shifter_7_overflow, not_1_out, or_1_out, xor_1_out;
  wire [7:0] absolute_value_1_out_2, absolute_value_2_out_2, additive_inverse_1_out_2, n7bit_shifter_1_out_3,
       n7bit_shifter_2_out_3, n7bit_shifter_3_out_3, n7bit_shifter_4_out_3, n7bit_shifter_5_out_3,
       n7bit_shifter_6_out_3, n7bit_shifter_7_out_3, n8bit_adder_1_out_3, n8bit_adder_2_out_3,
       n8bit_adder_3_out_3, n8bit_adder_4_out_3, n8bit_adder_5_out_3, n8bit_adder_6_out_3,
       n8bit_adder_7_out_3, n8x1_multiplier_1_out_3, n8x1_multiplier_2_out_3, n8x1_multiplier_3_out_3,
       n8x1_multiplier_4_out_3, n8x1_multiplier_5_out_3, n8x1_multiplier_6_out_3, n8x1_multiplier_7_out_3,
       n8x1_multiplier_8_out_3;

  Absolute_Value absolute_value_1 (
    .in_1(in_2), .out_2(absolute_value_1_out_2), .Is_it_negative(absolute_value_1_is_it_negative));
  Absolute_Value absolute_value_2 (
    .in_1(in_1), .out_2(absolute_value_2_out_2), .Is_it_negative(absolute_value_2_is_it_negative));
  _8x1_Multiplier u_8x1_multiplier_1 (
    .in_1(absolute_value_1_out_2[0]), .in_2(absolute_value_2_out_2), .out_3(n8x1_multiplier_1_out_3));
  _8x1_Multiplier u_8x1_multiplier_2 (
    .in_1(absolute_value_1_out_2[1]), .in_2(absolute_value_2_out_2), .out_3(n8x1_multiplier_2_out_3));
  _8x1_Multiplier u_8x1_multiplier_3 (
    .in_1(absolute_value_1_out_2[2]), .in_2(absolute_value_2_out_2), .out_3(n8x1_multiplier_3_out_3));
  _8x1_Multiplier u_8x1_multiplier_4 (
    .in_1(absolute_value_1_out_2[3]), .in_2(absolute_value_2_out_2), .out_3(n8x1_multiplier_4_out_3));
  _8x1_Multiplier u_8x1_multiplier_5 (
    .in_1(absolute_value_1_out_2[4]), .in_2(absolute_value_2_out_2), .out_3(n8x1_multiplier_5_out_3));
  _8x1_Multiplier u_8x1_multiplier_6 (
    .in_1(absolute_value_1_out_2[5]), .in_2(absolute_value_2_out_2), .out_3(n8x1_multiplier_6_out_3));
  _8x1_Multiplier u_8x1_multiplier_7 (
    .in_1(absolute_value_1_out_2[6]), .in_2(absolute_value_2_out_2), .out_3(n8x1_multiplier_7_out_3));
  _8x1_Multiplier u_8x1_multiplier_8 (
    .in_1(absolute_value_1_out_2[7]), .in_2(absolute_value_2_out_2), .out_3(n8x1_multiplier_8_out_3));
  _7bit_Shifter u_7bit_shifter_1 (
    .in_1(n8x1_multiplier_2_out_3), .in_2(4'b0001), .out_3(n7bit_shifter_1_out_3),
    .Overflow(n7bit_shifter_1_overflow));
  _7bit_Shifter u_7bit_shifter_2 (
    .in_1(n8x1_multiplier_3_out_3), .in_2(4'b0010), .out_3(n7bit_shifter_2_out_3),
    .Overflow(n7bit_shifter_2_overflow));
  _7bit_Shifter u_7bit_shifter_3 (
    .in_1(n8x1_multiplier_4_out_3), .in_2(4'b0011), .out_3(n7bit_shifter_3_out_3),
    .Overflow(n7bit_shifter_3_overflow));
  _7bit_Shifter u_7bit_shifter_4 (
    .in_1(n8x1_multiplier_5_out_3), .in_2(4'b0100), .out_3(n7bit_shifter_4_out_3),
    .Overflow(n7bit_shifter_4_overflow));
  _7bit_Shifter u_7bit_shifter_5 (
    .in_1(n8x1_multiplier_6_out_3), .in_2(4'b0101), .out_3(n7bit_shifter_5_out_3),
    .Overflow(n7bit_shifter_5_overflow));
  _7bit_Shifter u_7bit_shifter_6 (
    .in_1(n8x1_multiplier_7_out_3), .in_2(4'b0110), .out_3(n7bit_shifter_6_out_3),
    .Overflow(n7bit_shifter_6_overflow));
  _7bit_Shifter u_7bit_shifter_7 (
    .in_1(n8x1_multiplier_8_out_3), .in_2(4'b0111), .out_3(n7bit_shifter_7_out_3),
    .Overflow(n7bit_shifter_7_overflow));
  xor xor_1 (xor_1_out, absolute_value_2_is_it_negative, absolute_value_1_is_it_negative);
  _8bit_Adder u_8bit_adder_1 (
    .in_1(n8x1_multiplier_1_out_3), .in_2(n7bit_shifter_1_out_3), .out_3(n8bit_adder_1_out_3));  // open: Carry_Out, Overflow
  _8bit_Adder u_8bit_adder_2 (
    .in_1(n8bit_adder_1_out_3), .in_2(n7bit_shifter_2_out_3), .out_3(n8bit_adder_2_out_3));  // open: Carry_Out, Overflow
  _8bit_Adder u_8bit_adder_3 (
    .in_1(n8bit_adder_2_out_3), .in_2(n7bit_shifter_3_out_3), .out_3(n8bit_adder_3_out_3));  // open: Carry_Out, Overflow
  _8bit_Adder u_8bit_adder_4 (
    .in_1(n8bit_adder_3_out_3), .in_2(n7bit_shifter_4_out_3), .out_3(n8bit_adder_4_out_3));  // open: Carry_Out, Overflow
  _8bit_Adder u_8bit_adder_5 (
    .in_1(n8bit_adder_4_out_3), .in_2(n7bit_shifter_5_out_3), .out_3(n8bit_adder_5_out_3));  // open: Carry_Out, Overflow
  _8bit_Adder u_8bit_adder_6 (
    .in_1(n8bit_adder_5_out_3), .in_2(n7bit_shifter_6_out_3), .out_3(n8bit_adder_6_out_3));  // open: Carry_Out, Overflow
  _8bit_Adder u_8bit_adder_7 (
    .in_1(n8bit_adder_6_out_3), .in_2(n7bit_shifter_7_out_3), .out_3(n8bit_adder_7_out_3));  // open: Carry_Out, Overflow
  Additive_Inverse additive_inverse_1 (
    .in_1(n8bit_adder_7_out_3), .out_2(additive_inverse_1_out_2), .Overflow(additive_inverse_1_overflow));
  or or_1 (or_1_out, n7bit_shifter_1_overflow, n7bit_shifter_2_overflow, n7bit_shifter_3_overflow, n7bit_shifter_4_overflow, n7bit_shifter_5_overflow, n7bit_shifter_6_overflow, n7bit_shifter_7_overflow);
  Multiplexer #(.width(8), .enable("false")) multiplexer_1 (
    .in0(n8bit_adder_7_out_3), .in1(additive_inverse_1_out_2), .out(out_3), .sel(xor_1_out));
  not not_1 (not_1_out, xor_1_out);
  and and_1 (and_1_out, additive_inverse_1_overflow, not_1_out);
  or or_2 (Overflow, and_1_out, or_1_out);
endmodule

// Shift
module _8bit_Shifter (
  input  [7:0] in_1,
  input  [3:0] in_2,
  output [7:0] out_3,
  output Overflow
);

  wire [15:8] shifter_1_out;

  Shifter #(.width(16)) shifter_1 (.in({{8{1'b0}}, in_1}), .\dist (in_2), .out({shifter_1_out, out_3}));
  or or_1 (Overflow, shifter_1_out[8], shifter_1_out[9], shifter_1_out[10], shifter_1_out[11], shifter_1_out[12], shifter_1_out[13], shifter_1_out[14], shifter_1_out[15]);
endmodule

// Div
module _8bit_Divider (
  input  [7:0] in_1,
  input  [7:0] in_2,
  input  Option,
  output [7:0] out_4,
  output Overflow
);

  wire absolute_value_1_is_it_negative, absolute_value_2_is_it_negative, additive_inverse_1_overflow,
       multiplexer_11_out, n7bit_shifter_1_overflow, n7bit_shifter_2_overflow, n7bit_shifter_3_overflow,
       n7bit_shifter_4_overflow, n7bit_shifter_5_overflow, n7bit_shifter_6_overflow,
       n8bit_shifter_1_overflow, not_1_out, not_3_out, xor_1_out;
  wire [7:0] absolute_value_1_out_2, absolute_value_2_out_2, additive_inverse_1_out_2, multiplexer_1_out,
       multiplexer_2_out, multiplexer_3_out, multiplexer_4_out, multiplexer_5_out, multiplexer_6_out,
       multiplexer_7_out, multiplexer_8_out, multiplexer_9_out, multiplexer_10_out, multiplexer_12_out,
       multiplexer_13_out, multiplexer_14_out, multiplexer_15_out, multiplexer_16_out, multiplexer_18_out,
       n7bit_shifter_1_out_3, n7bit_shifter_2_out_3, n7bit_shifter_3_out_3, n7bit_shifter_4_out_3,
       n7bit_shifter_5_out_3, n7bit_shifter_6_out_3, n8bit_shifter_1_out_3, n8bit_subtractor_1_out_3,
       n8bit_subtractor_2_out_3, n8bit_subtractor_3_out_3, n8bit_subtractor_4_out_3,
       n8bit_subtractor_5_out_3, n8bit_subtractor_6_out_3, n8bit_subtractor_7_out_3,
       n8bit_subtractor_8_out_3, not_2_out;

  Absolute_Value absolute_value_1 (
    .in_1(in_1), .out_2(absolute_value_1_out_2), .Is_it_negative(absolute_value_1_is_it_negative));
  Absolute_Value absolute_value_2 (
    .in_1(in_2), .out_2(absolute_value_2_out_2), .Is_it_negative(absolute_value_2_is_it_negative));
  _8bit_Shifter u_8bit_shifter_1 (
    .in_1(absolute_value_2_out_2), .in_2(4'b0111), .out_3(n8bit_shifter_1_out_3),
    .Overflow(n8bit_shifter_1_overflow));
  _7bit_Shifter u_7bit_shifter_1 (
    .in_1(absolute_value_2_out_2), .in_2(4'b0110), .out_3(n7bit_shifter_1_out_3),
    .Overflow(n7bit_shifter_1_overflow));
  _7bit_Shifter u_7bit_shifter_2 (
    .in_1(absolute_value_2_out_2), .in_2(4'b0101), .out_3(n7bit_shifter_2_out_3),
    .Overflow(n7bit_shifter_2_overflow));
  _7bit_Shifter u_7bit_shifter_3 (
    .in_1(absolute_value_2_out_2), .in_2(4'b0100), .out_3(n7bit_shifter_3_out_3),
    .Overflow(n7bit_shifter_3_overflow));
  _7bit_Shifter u_7bit_shifter_4 (
    .in_1(absolute_value_2_out_2), .in_2(4'b0011), .out_3(n7bit_shifter_4_out_3),
    .Overflow(n7bit_shifter_4_overflow));
  Multiplexer #(.width(8), .enable("false")) multiplexer_1 (
    .in0(n8bit_shifter_1_out_3), .in1({8{1'b0}}), .out(multiplexer_1_out), .sel(n8bit_shifter_1_overflow));
  Multiplexer #(.width(8), .enable("false")) multiplexer_2 (
    .in0(n7bit_shifter_1_out_3), .in1({8{1'b0}}), .out(multiplexer_2_out), .sel(n7bit_shifter_1_overflow));
  Multiplexer #(.width(8), .enable("false")) multiplexer_3 (
    .in0(n7bit_shifter_2_out_3), .in1({8{1'b0}}), .out(multiplexer_3_out), .sel(n7bit_shifter_2_overflow));
  Multiplexer #(.width(8), .enable("false")) multiplexer_4 (
    .in0(n7bit_shifter_3_out_3), .in1({8{1'b0}}), .out(multiplexer_4_out), .sel(n7bit_shifter_3_overflow));
  _7bit_Shifter u_7bit_shifter_5 (
    .in_1(absolute_value_2_out_2), .in_2(4'b0010), .out_3(n7bit_shifter_5_out_3),
    .Overflow(n7bit_shifter_5_overflow));
  _7bit_Shifter u_7bit_shifter_6 (
    .in_1(absolute_value_2_out_2), .in_2(4'b0001), .out_3(n7bit_shifter_6_out_3),
    .Overflow(n7bit_shifter_6_overflow));
  _8bit_Subtractor u_8bit_subtractor_1 (
    .in_1(absolute_value_1_out_2), .in_2(multiplexer_1_out), .out_3(n8bit_subtractor_1_out_3));  // open: Overflow
  _8bit_Subtractor u_8bit_subtractor_2 (
    .in_1(multiplexer_8_out), .in_2(multiplexer_2_out), .out_3(n8bit_subtractor_2_out_3));  // open: Overflow
  _8bit_Subtractor u_8bit_subtractor_3 (
    .in_1(multiplexer_9_out), .in_2(multiplexer_3_out), .out_3(n8bit_subtractor_3_out_3));  // open: Overflow
  _8bit_Subtractor u_8bit_subtractor_4 (
    .in_1(multiplexer_10_out), .in_2(multiplexer_4_out), .out_3(n8bit_subtractor_4_out_3));  // open: Overflow
  Multiplexer #(.width(8), .enable("false")) multiplexer_5 (
    .in0(n7bit_shifter_4_out_3), .in1({8{1'b0}}), .out(multiplexer_5_out), .sel(n7bit_shifter_4_overflow));
  Multiplexer #(.width(8), .enable("false")) multiplexer_6 (
    .in0(n7bit_shifter_5_out_3), .in1({8{1'b0}}), .out(multiplexer_6_out), .sel(n7bit_shifter_5_overflow));
  Multiplexer #(.width(8), .enable("false")) multiplexer_7 (
    .in0(n7bit_shifter_6_out_3), .in1({8{1'b0}}), .out(multiplexer_7_out), .sel(n7bit_shifter_6_overflow));
  xor xor_1 (xor_1_out, absolute_value_1_is_it_negative, absolute_value_2_is_it_negative);
  _8bit_Subtractor u_8bit_subtractor_5 (
    .in_1(multiplexer_12_out), .in_2(multiplexer_5_out), .out_3(n8bit_subtractor_5_out_3));  // open: Overflow
  _8bit_Subtractor u_8bit_subtractor_6 (
    .in_1(multiplexer_13_out), .in_2(multiplexer_6_out), .out_3(n8bit_subtractor_6_out_3));  // open: Overflow
  _8bit_Subtractor u_8bit_subtractor_7 (
    .in_1(multiplexer_14_out), .in_2(multiplexer_7_out), .out_3(n8bit_subtractor_7_out_3));  // open: Overflow
  _8bit_Subtractor u_8bit_subtractor_8 (
    .in_1(multiplexer_15_out), .in_2(absolute_value_2_out_2), .out_3(n8bit_subtractor_8_out_3));  // open: Overflow
  Multiplexer #(.width(8), .enable("false")) multiplexer_8 (
    .in0(n8bit_subtractor_1_out_3), .in1(absolute_value_1_out_2), .out(multiplexer_8_out),
    .sel(n8bit_subtractor_1_out_3[7]));
  Multiplexer #(.width(8), .enable("false")) multiplexer_9 (
    .in0(n8bit_subtractor_2_out_3), .in1(multiplexer_8_out), .out(multiplexer_9_out),
    .sel(n8bit_subtractor_2_out_3[7]));
  Multiplexer #(.width(8), .enable("false")) multiplexer_10 (
    .in0(n8bit_subtractor_3_out_3), .in1(multiplexer_9_out), .out(multiplexer_10_out),
    .sel(n8bit_subtractor_3_out_3[7]));
  Multiplexer #(.enable("false")) multiplexer_11 (
    .in0(absolute_value_1_is_it_negative), .in1(xor_1_out), .out(multiplexer_11_out), .sel(not_1_out));
  not not_1 (not_1_out, Option);
  Multiplexer #(.width(8), .enable("false")) multiplexer_12 (
    .in0(n8bit_subtractor_4_out_3), .in1(multiplexer_10_out), .out(multiplexer_12_out),
    .sel(n8bit_subtractor_4_out_3[7]));
  Multiplexer #(.width(8), .enable("false")) multiplexer_13 (
    .in0(n8bit_subtractor_5_out_3), .in1(multiplexer_12_out), .out(multiplexer_13_out),
    .sel(n8bit_subtractor_5_out_3[7]));
  Multiplexer #(.width(8), .enable("false")) multiplexer_14 (
    .in0(n8bit_subtractor_6_out_3), .in1(multiplexer_13_out), .out(multiplexer_14_out),
    .sel(n8bit_subtractor_6_out_3[7]));
  Multiplexer #(.width(8), .enable("false")) multiplexer_15 (
    .in0(n8bit_subtractor_7_out_3), .in1(multiplexer_14_out), .out(multiplexer_15_out),
    .sel(n8bit_subtractor_7_out_3[7]));
  nor nor_1 (not_2_out[7], n8bit_subtractor_1_out_3[7], n8bit_shifter_1_overflow);
  nor nor_2 (not_2_out[6], n8bit_subtractor_2_out_3[7], n7bit_shifter_1_overflow);
  nor nor_3 (not_2_out[5], n8bit_subtractor_3_out_3[7], n7bit_shifter_2_overflow);
  nor nor_4 (not_2_out[4], n8bit_subtractor_4_out_3[7], n7bit_shifter_3_overflow);
  Multiplexer #(.width(8), .enable("false")) multiplexer_16 (
    .in0(n8bit_subtractor_8_out_3), .in1(multiplexer_15_out), .out(multiplexer_16_out),
    .sel(n8bit_subtractor_8_out_3[7]));
  Additive_Inverse additive_inverse_1 (
    .in_1(multiplexer_18_out), .out_2(additive_inverse_1_out_2), .Overflow(additive_inverse_1_overflow));
  nor nor_5 (not_2_out[3], n8bit_subtractor_5_out_3[7], n7bit_shifter_4_overflow);
  nor nor_6 (not_2_out[2], n8bit_subtractor_6_out_3[7], n7bit_shifter_5_overflow);
  nor nor_7 (not_2_out[1], n8bit_subtractor_7_out_3[7], n7bit_shifter_6_overflow);
  not not_2 (not_2_out[0], n8bit_subtractor_8_out_3[7]);
  Multiplexer #(.width(8), .enable("false")) multiplexer_17 (
    .in0(multiplexer_18_out), .in1(additive_inverse_1_out_2), .out(out_4), .sel(multiplexer_11_out));
  not not_3 (not_3_out, multiplexer_11_out);
  and and_1 (Overflow, additive_inverse_1_overflow, not_3_out);
  Multiplexer #(.width(8), .enable("false")) multiplexer_18 (
    .in0(not_2_out), .in1(multiplexer_16_out), .out(multiplexer_18_out), .sel(Option));
endmodule

module main (
);

  RAM ram_1 ();  // open: addr, data, sel, clk, ld, clr
  Program_Counter PC ();
  Control CTRL ();
  Instruction_Register IR ();
  Accumulator ACC ();
endmodule

module Program_Counter (
);

  _8bit_Divider u_8bit_divider_1 ();  // open: in_1, in_2, Option, out_4, Overflow
endmodule
